# Fritzing sketch sploder (saved by Fritzing 0.9.1b)
breadboards: 1

parts:
  Arduino = Arduino Pro Mini v13
  R1 = Resistor [tolerance=±5% resistance=10k package=THT]
  S1 = Pushbutton [package="[THT]"]
  LIPO_(1_cell_400mAh) = DC Power [voltage=3.7V]
  S2 = Toggle Switch [package=THT]
  R2 = Resistor [tolerance=±5% resistance=220 package=THT]
  R3 = Resistor [tolerance=±5% resistance=1k package=THT]
  Arming_LED = LED - 5mm [color="Red (633nm)" package="5 mm [THT]"]
  Firing_LED = LED - 5mm [color="Red (633nm)" package="5 mm [THT]"]
  nrf8001_Breakout = nRF8001 Bluetooth LE Breakout

nets:
  VCC: Arduino.VCC, nrf8001_Breakout.VIN
  GND: Arduino.GND, R1.Pin_1, S2.L2, R2.Pin_1, R3.Pin_1, nrf8001_Breakout.GND
  N1: Arduino.RAW, Arduino.D3_PWM, S1.Pin_3, S1.Pin_4, LIPO_(1_cell_400mAh).V-
  N2: Arduino.D13/SCK, nrf8001_Breakout.SCK
  N3: Arduino.D12/MISO, nrf8001_Breakout.MISO
  N4: Arduino.D11_PWM/MOSI, nrf8001_Breakout.MOSI
  N5: Arduino.D10_PWM/SS, nrf8001_Breakout.REQ
  N6: Arduino.D9_PWM, nrf8001_Breakout.RST
  N7: Arduino.D8, S2.COM
  N8: Arduino.D5_PWM, Firing_LED.anode
  N9: Arduino.D4, Arming_LED.anode
  N10: Arduino.D2, nrf8001_Breakout.RDY
  N11: R1.Pin_0, S1.Pin_2
  N12: R2.Pin_0, Arming_LED.cathode
  N13: R3.Pin_0, Firing_LED.cathode

notes:
  Sploder
  A connected button for doing stuff.

custom parts:
  nRF8001 Bluetooth LE Breakout: nRF8001 Breakout Board
